// Logisim project masina_de_spalat.circ as structural Verilog
module main (
  input  in_1,
  input  in_2,
  input  in_3,
  input  in_4,
  input  in_5,
  input  in_6,
  input  in_7,
  input  in_8,
  input  in_9,
  input  in_10,
  input  in_11,
  input  in_12,
  input  in_13,
  input  in_14,
  input  in_15,
  input  in_16,
  input  in_17,
  output out_18,
  output [8:0] out_19
);

  wire binary_to_bcd_converter_1_p2, binary_to_bcd_converter_1_p3, binary_to_bcd_converter_2_p2,
       binary_to_bcd_converter_2_p3, button_1_out, clock_1_out, clock_2_out, clock_3_out, counter_1_cen,
       counter_1_clat_p, counter_1_clat_s, counter_1_h, counter_1_presp, counter_1_sp_p, cu_1_led_30,
       cu_1_led_40, cu_1_led_60, cu_1_led_90, cu_1_led_800, cu_1_led_1000, cu_1_led_1200, cu_1_led_am,
       cu_1_led_cs, cu_1_led_doorlock, cu_1_led_pr, debouncer_1_enable;
  wire [8:0] counter_1_init, counter_1_timp;

  Button button_1 (.out(button_1_out));
  Clock clock_1 (.out(clock_1_out));
  CU cu_1 (
    .clk(clock_1_out), .ok(button_1_out), .am(in_1), .t_30(in_2), .t_40(in_3), .t_60(in_4), .t_90(in_5),
    .v_800(in_6), .v_1000(in_7), .v_1200(in_8), .PR(in_9), .CS(in_10), .SR(in_11), .CAM(in_12), .CI(in_13),
    .RM(in_14), .AA(in_15), .start(in_16), .reset(in_17), .led_am(cu_1_led_am), .led_30(cu_1_led_30),
    .led_40(cu_1_led_40), .led_60(cu_1_led_60), .led_90(cu_1_led_90), .led_800(cu_1_led_800),
    .led_1000(cu_1_led_1000), .led_1200(cu_1_led_1200), .led_PR(cu_1_led_pr), .led_CS(cu_1_led_cs),
    .led_doorlock(cu_1_led_doorlock), .stare(out_19));
  LED led_1 (.in(cu_1_led_am));
  LED led_2 (.in(cu_1_led_30));
  LED led_3 (.in(cu_1_led_40));
  LED led_4 (.in(cu_1_led_60));
  LED led_5 (.in(cu_1_led_90));
  LED led_6 (.in(cu_1_led_800));
  LED led_7 (.in(cu_1_led_1000));
  LED led_8 (.in(cu_1_led_1200));
  LED led_9 (.in(cu_1_led_cs));
  LED led_10 (.in(cu_1_led_pr));
  Clock clock_2 (.out(clock_2_out));
  LED led_11 (.in(cu_1_led_doorlock));
  debouncer debouncer_1 (.btn(cu_1_led_doorlock), .clk(clock_2_out), .enable(debouncer_1_enable));
  Clock clock_3 (.out(clock_3_out));
  LED led_12 (.in(counter_1_h));
  COUNTER counter_1 (
    .CLK1S(clock_3_out), .T30(cu_1_led_30), .T40(cu_1_led_40), .T60(cu_1_led_60), .T90(cu_1_led_90),
    .PR(cu_1_led_pr), .CS(cu_1_led_cs), .EN(debouncer_1_enable), .PRESP(counter_1_presp), .H(counter_1_h),
    .SP_P(counter_1_sp_p), .CLAT_P(counter_1_clat_p), .CLAT_S(counter_1_clat_s), .CEN(counter_1_cen),
    .DO(out_18), .TIMP(counter_1_timp), .INIT(counter_1_init));
  LED led_13 (.in(counter_1_presp));
  LED led_14 (.in(counter_1_sp_p));
  LED led_15 (.in(counter_1_clat_p));
  LED led_16 (.in(counter_1_clat_s));
  LED led_17 (.in(counter_1_cen));
  // Binary_to_BCD_converter binary_to_bcd_converter_1: pin names not known; wires that end beside it: counter_1_timp, binary_to_bcd_converter_1_p2, binary_to_bcd_converter_1_p3
  _7_Segment_Display u_7_segment_display_1 ();  // open: g, f, a, b, e, d, c, dp
  // BCD_to_7_Segment_decoder bcd_to_7_segment_decoder_1: pin names not known; wires that end beside it: binary_to_bcd_converter_1_p2
  _7_Segment_Display u_7_segment_display_2 ();  // open: g, f, a, b, e, d, c, dp
  // BCD_to_7_Segment_decoder bcd_to_7_segment_decoder_2: pin names not known; wires that end beside it: binary_to_bcd_converter_1_p3
  // Binary_to_BCD_converter binary_to_bcd_converter_2: pin names not known; wires that end beside it: counter_1_init, binary_to_bcd_converter_2_p2, binary_to_bcd_converter_2_p3
  _7_Segment_Display u_7_segment_display_3 ();  // open: g, f, a, b, e, d, c, dp
  // BCD_to_7_Segment_decoder bcd_to_7_segment_decoder_3: pin names not known; wires that end beside it: binary_to_bcd_converter_2_p2
  _7_Segment_Display u_7_segment_display_4 ();  // open: g, f, a, b, e, d, c, dp
  // BCD_to_7_Segment_decoder bcd_to_7_segment_decoder_4: pin names not known; wires that end beside it: binary_to_bcd_converter_2_p3

  // Notes on the sheet:
  //   A/M
  //   30
  //   40
  //   60
  //   90
  //   800
  //   1000
  //   1200
  //   CS
  //   PR
  //   DOOR LOCK
endmodule

// VHDL entity CU, as the project stores it:
--------------------------------------------------------------------------------
-- Project :
-- File    :
-- Autor   :
-- Date    :
--
--------------------------------------------------------------------------------
-- Description :
--
--------------------------------------------------------------------------------

LIBRARY ieee;
USE ieee.std_logic_1164.all;

ENTITY CU IS
  PORT (
clk: in std_logic;
        ok: in std_logic;
        am: in std_logic;    ---0 automat, 1 manual
        t_30,t_40,t_60,t_90: in std_logic;
        v_800,v_1000,v_1200: in std_logic;
        PR: in std_logic;           
        CS: in std_logic;
        SR,CAM,CI,RM,AA: in std_logic;
        start: in std_logic;
        reset: in std_logic;
        led_am, led_30,led_40,led_60,led_90,led_800,led_1000,led_1200,led_PR,led_CS,led_doorlock: out std_logic;
        stare: out std_logic_vector(8 downto 0)
        
    );
END CU;

--------------------------------------------------------------------------------
--Complete your VHDL description below
--------------------------------------------------------------------------------

ARCHITECTURE TypeArchitecture OF CU IS


type program_t is (PU,PSR,PCAM,PCI,PRM,PAA);
signal PROGRAM: program_t:=PU;

type state is (idle,a,c,j,o,q,p,n);
signal current_state, next_state: state:=idle;

type temperatura_t is (tU,t30,t40,t60,t90);
signal TEMP: temperatura_t:=tU;

type viteza_t is (vU,v800,v1000,v1200);
signal VIT: viteza_t:=vU;

signal AUT_MAN: std_logic:='0';                 --0 automat, 1 manual

signal PRESP: std_logic:='0';
signal CLSUP: std_logic:='0';

signal EN_DOOR: std_logic:='0';

signal temperatura: std_logic_vector(3 downto 0);
signal viteza: std_logic_vector(2 downto 0);
signal programe: std_logic_vector(4 downto 0);




BEGIN

--------------------------------------------- mux for temperatura
temperatura<=t_90 & t_60 & t_40 & t_30;
---------------------------------------------  mux for viteza
viteza<=v_1200 & v_1000 & v_800;
--------------------------------------------- mux for programe
programe<=AA & RM & CI & CAM & SR;
---------------------------------------------transition process

transition:process (clk)
begin
if rising_edge(clk) then
current_state<=next_state;
end if;
end process;

---------------------------------------------next state process / inputs
stare_urmatoare: process (temperatura, viteza, programe, ok, PR,CS,am,current_state)
begin
case current_state is
---------------------------------------------- state idle
when idle => 
       PROGRAM<=PU;
       TEMP<=tU;
        VIT<=vU;
        PRESP<='0';
        CLSUP<='0';
        EN_DOOR<='0';
          if ok='1' then 
            if am='1' then
                AUT_MAN<='1';
                next_state<=a;
             else
               next_state<=q;
                end if;
            else
                next_state<=idle;
            end if;
----------------------------------------------- state a
 when a =>
 case temperatura is
 ----------------------------------------------- temp 30
    when "0001" =>
        if ok='1' then
           TEMP<=t30;
           next_state<=c;
         else
            next_state<=a;
        end if;
------------------------------------------------ temp 40
    when "0010" =>
         if ok='1' then
             TEMP<=t40;
             next_state<=c;
         else
             next_state<=a;
          end if;
---------------------------------------------- temp 60
    when "0100" =>
         if ok='1' then
             TEMP<=t60;
             next_state<=c;
         else
             next_state<=a;
          end if;
---------------------------------------------- temp 90
        when "1000" => 
          if ok='1' then
             TEMP<=t90;
             next_state<=c;
         else
             next_state<=a;
          end if;
        when others => next_state<=a;
end case;
------------------------------------------------ stare c
     when c=>
     case viteza is
----------------------------------------------- vit 800
        when "001" =>
           if ok='1' then
           VIT<=v800;
           next_state<=j;
           else
              next_state<=c;
         end if;
------------------------------------------------ vit 1000
        when "010" => 
           if ok='1'  then
              VIT<=v1000;
               next_state<=j;
           else
               next_state<=c;
           end if;
------------------------------------------------- vit 1200
           when "100" =>
             if ok='1' then
               VIT<=v1200;
                next_state<=j;
             else
               next_state<=c;
              end if;
              
 when others=> next_state<=c;
 end case;
--------------------------------------------------- stare j
when j => 
if ok='1'  then 
 if PR='0' then    
     next_state<=n;
 else
     PRESP<='1';
     next_state<=n;
  end if;
 else 
    next_state<=j;
end if;
---------------------------------------------------- stare n
when n => 
if ok='1'  then 
 if CS='0' then    
     next_state<=o;
 else
     CLSUP<='1';
     next_state<=o;
  end if;
 else 
    next_state<=n;
end if;
---------------------------------------------------- stare q
when q => 
case programe is
-------------------------------------------------------spalare rapida 
when "00001" => 
        if ok='1'  then
          PROGRAM<=PSR;
          TEMP<=t30;
          VIT<=v1200;
           next_state<=o;
         else
          next_state<=q;
         end if;
----------------------------------------------------- camasi
when "00010" => 
      if ok='1'   then          
           PROGRAM<=PCAM;
           TEMP<=t40;
           VIT<=v800;
           next_state<=o;
        else
            next_state<=q;
        end if;
---------------------------------------------------- culori inchise
when "00100" => 
       if ok='1'   then          
           PROGRAM<=PCI;
           TEMP<=t40;
           VIT<=v1000;
           CLSUP<='1';
           next_state<=o;
        else
            next_state<=q;
        end if;
-------------------------------------------------------- rufe murdare
when "01000" => 
      if ok='1'   then          
           PROGRAM<=PRM;
           TEMP<=t40;
           VIT<=v1000;
           PRESP<='1';
           CLSUP<='1';
           next_state<=o;
        else
            next_state<=q;
        end if;
------------------------------------------------------ anti alergice
when "10000" => 
      if ok='1'   then          
           PROGRAM<=PAA;
           TEMP<=t90;
           VIT<=v1200;
           CLSUP<='1';
           next_state<=o;
        else
            next_state<=q;
        end if;
when others=> next_state<=q;
end case;
------------------------------------------------------ stare o
when o =>
  if start ='0' then
       if reset='1'then
            next_state<=idle;
       end if;
       else
       if ok='1' then
            next_state<=p;
        end if;
   end if;
---------------------------------------------------- stare p
when p =>  EN_DOOR<='1';

end case;
end process;


ouptuts: process (current_state)
begin
stare<="000000000";
case current_state is
when idle=> stare(8)<='1';
 led_am<='0'; led_30<='0';led_40<='0';led_60<='0';led_90<='0';led_800<='0';led_1000<='0';led_1200<='0';led_PR<='0';led_CS<='0';led_doorlock<='0';
when a=> stare(7)<='1';
         led_am<='1';
         
when c=> stare(6)<='1';
         case TEMP is
         when t30=> led_30<='1';
         when t40=> led_40<='1';
         when t60=> led_60<='1';
         when t90=> led_90<='1';
         when others=> 
         end case;
         
when j=> stare(5)<='1';
          case VIT is
         when v800=> led_800<='1';
         when v1000=> led_1000<='1';
         when v1200=> led_1200<='1';
         when others=>
         end case;
         
when n=> stare(4)<='1';
         if PRESP='1' then 
            led_PR<='1'; 
         end if;
         
when q=> stare(3)<='1';
         if CLSUP='1' then 
            led_CS<='1'; 
         end if;
         
when o=>stare(3)<='1';
         if CLSUP='1' then 
            led_CS<='1'; 
         end if;
        stare(2)<='1';
        case PROGRAM is 
         when PSR =>
         led_30<='1';
         led_1200<='1';
         when PCAM =>
         led_60<='1';
         led_800<='1';
         when PCI=>
         led_40<='1';
         led_1000<='1';
         led_CS<='1';
         when PRM=>
         led_40<='1';
         led_1000<='1';
         led_PR<='1';
         when PAA=>
         led_90<='1';
         led_1200<='1';
         led_CS<='1';
         when others=>
         end case;
when p=> stare(1)<='1';
led_doorlock<='1';
end case;
end process;

END TypeArchitecture;

// VHDL entity COUNTER, as the project stores it:
--------------------------------------------------------------------------------
-- Project :
-- File    :
-- Autor   :
-- Date    :
--
--------------------------------------------------------------------------------
-- Description :
--
--------------------------------------------------------------------------------

LIBRARY ieee;
USE ieee.std_logic_1164.all;
use ieee.std_logic_unsigned.all;
use ieee.std_logic_arith.all;
use ieee.numeric_std.all;

ENTITY COUNTER IS
  PORT ( CLK1S: in std_logic;
         T30,T40,T60,T90: in std_logic;
         PR,CS: in std_logic;
         EN: in std_logic;
         PRESP, H , SP_P, CLAT_P, CLAT_S, CEN, DO: out std_logic;
         TIMP: out std_logic_vector(8 downto 0);
         INIT: out std_logic_vector(8 downto 0)
         
    );
END COUNTER;

--------------------------------------------------------------------------------
--Complete your VHDL description below
--------------------------------------------------------------------------------

ARCHITECTURE TypeArchitecture OF COUNTER IS

signal COUNT: std_logic_vector(8 downto 0):=(others=>'0');
signal INITIAL_VALUE: std_logic_vector(8 downto 0):=(others=>'0');
signal THPR,TPR,THSP, TCS: integer:=0;
signal TSP: integer:=20;
signal TCP, TC: integer:=10;



signal temperatura: std_logic_vector(4 downto 0);


BEGIN
INIT<=INITIAL_VALUE;
temperatura<=PR & T90 & T60 & T40 & T30;


with temperatura select THPR<=1 when "10100",
                              2 when "11000",
                              0 when others;

with temperatura(3 downto 0) select THSP<=1 when "0100",
                                          2 when "1000",
                                          0 when others;
                                       
TPR<=10 when PR='1';
TCS<=10 when CS='1';

--COUNT<=std_logic_vector(to_unsigned(THPR+TPR+THSP+TSP+TCP+TCS+TC,9)) when EN_INT='1';




process(CLK1S,EN)
begin
	if EN='1' then
		COUNT<=std_logic_vector(to_unsigned(THPR+TPR+THSP+TSP+TCP+TCS+TC,9));
		INITIAL_VALUE<=COUNT;
	elsif rising_edge(CLK1S) and  COUNT/="000000000" then 
	COUNT<=COUNT-1;
	end if;
end process;

process(COUNT)
begin
	if COUNT>0 then
		if conv_integer(COUNT)>conv_integer(INITIAL_VALUE)-THPR then
		PRESP<='0'; H<='1'; SP_P<='0'; CLAT_P<='0'; CLAT_S<='0'; CEN<='0'; 
		elsif conv_integer(COUNT)>conv_integer(INITIAL_VALUE)-THPR-TPR then
		PRESP<='1'; H<='0'; SP_P<='0'; CLAT_P<='0'; CLAT_S<='0'; CEN<='0'; 
		elsif  conv_integer(COUNT)>conv_integer(INITIAL_VALUE)-THPR-TPR-THSP then
		PRESP<='0'; H<='1'; SP_P<='0'; CLAT_P<='0'; CLAT_S<='0'; CEN<='0'; 
		elsif  conv_integer(COUNT)>conv_integer(INITIAL_VALUE)-THPR-TPR-THSP-TSP then
		PRESP<='0'; H<='0'; SP_P<='1'; CLAT_P<='0'; CLAT_S<='0'; CEN<='0'; 
		elsif  conv_integer(COUNT)>conv_integer(INITIAL_VALUE)-THPR-TPR-THSP-TSP-TCP then
		PRESP<='0'; H<='0'; SP_P<='0'; CLAT_P<='1'; CLAT_S<='0'; CEN<='0'; 
		elsif  conv_integer(COUNT)>conv_integer(INITIAL_VALUE)-THPR-TPR-THSP-TSP-TCP-TCS then
		PRESP<='0'; H<='0'; SP_P<='0'; CLAT_P<='0'; CLAT_S<='1'; CEN<='0'; DO<='0';
		elsif  conv_integer(COUNT)>conv_integer(INITIAL_VALUE)-THPR-TPR-THSP-TSP-TCP-TCS-TC then
		PRESP<='0'; H<='0'; SP_P<='0'; CLAT_P<='0'; CLAT_S<='0'; CEN<='1'; 
		end if;
	else
		PRESP<='0'; H<='0'; SP_P<='0'; CLAT_P<='0'; CLAT_S<='0'; CEN<='0';
	end if;
end process;

DO<='1' when conv_integer(COUNT)=0 else '0'; 

TIMP<=COUNT;

END TypeArchitecture;

// VHDL entity debouncer, as the project stores it:
library IEEE;
use IEEE.STD_LOGIC_1164.ALL;
use IEEE.STD_LOGIC_UNSIGNED.ALL;

-- Uncomment the following library declaration if using
-- arithmetic functions with Signed or Unsigned values
--use IEEE.NUMERIC_STD.ALL;

-- Uncomment the following library declaration if instantiating
-- any Xilinx primitives in this code.
--library UNISIM;
--use UNISIM.VComponents.all;

entity debouncer is
    Port ( btn : in  STD_LOGIC;
           clk : in  STD_LOGIC;
           enable : out  STD_LOGIC);
end debouncer;

architecture Behavioral of debouncer is
signal q1,q2,q3:std_logic;
signal counter:std_logic_vector(1 downto 0):="00";

begin

enable<=q2 and (not(q3));

process(clk)
begin
if rising_edge(clk) then counter<=counter+1;
end if;

end process;

process(clk)
begin
if rising_edge(clk) then
    if (counter(1 downto 0))="11" then q1<=btn;
	 end if;
	 end if;
end process;


process(clk)
begin
	if rising_edge(clk) then
	q2<=q1;
	q3<=q2;
	end if;


end process;

end Behavioral;

// VHDL entity frequency_divider, as the project stores it:
library IEEE;
use IEEE.STD_LOGIC_1164.ALL;

entity frequency_divider is
    Port ( clk : in  STD_LOGIC;
           rst : in  STD_LOGIC;
           divided_clk : out  STD_LOGIC);
end frequency_divider;

architecture Behavioral of frequency_divider is
signal counter:integer:=1;
signal new_clk:std_logic:='0';


begin

process(clk,rst)
begin
if rst='1' then counter<=1;
elsif clk='1' and clk'event then
	if counter=50000000 then
		counter<=1;
		new_clk<=not(new_clk);
	else
		counter<=counter+1;
	end if;
end if;
end process;
-- now new_clk can be used as input clk for another components
divided_clk<=new_clk;


end Behavioral;
